# Fritzing sketch Osciloscopio (saved by Fritzing 0.9.3b)
breadboards: 1

parts:
  LCD1 = LCD screen
  Componente1 = Arduino Uno (Rev3)
  R1 = Rotary Potentiometer (Small) [maximum_resistance=100kΩ package=THT]
  Componente2 = Bluetooth HC-05 Macho
  R2 = TRIMPOT [package=trim_pot_pth]

nets:
  GND: LCD1.VSS, LCD1.R/W, LCD1.LED-, Componente1.GND, R1.leg1, Componente2.GND, R2.CCW
  VDD: LCD1.VDD, LCD1.LED+, Componente1.5V, R1.leg2, Componente2.VCC, R2.CW
  N1: LCD1.V0, R1.wiper
  N2: LCD1.RS, Componente1.D2
  N3: LCD1.E, Componente1.D3_PWM
  N4: LCD1.DB4, Componente1.D4
  N5: LCD1.DB5, Componente1.D5_PWM
  N6: LCD1.DB6, Componente1.D6_PWM
  N7: LCD1.DB7, Componente1.D7
  N8: Componente1.A0, R2.WIPER
  N9: Componente1.D0/RX, Componente2.TXD
  N10: Componente1.D1/TX, Componente2.RXD
